// Logisim project circ_processador.circ as structural Verilog: 12 circuits, main circuit main
module main (
  input  [3:0] A,
  input  [3:0] OPERANDO,
  input  DIRECIONADOR,
  input  [2:0] DECODIFICADOR,
  output OVERFLOW,
  output ZERO,
  output [3:0] SAIDA
);

  ULA ula_1 (
    .DIRECIONADOR(DIRECIONADOR), .B(OPERANDO), .A(A), .OVERFLOW(OVERFLOW), .OPERADOR(DECODIFICADOR),
    .ZERO(ZERO), .SAIDA(SAIDA));
endmodule

module ADD_UM (
  input  A,
  input  B,
  input  VEM_1,
  output Soma,
  output Vai_1
);

  wire and_1_out, and_2_out, and_3_out, and_4_out, and_5_out, and_6_out, and_7_out, not_1_out, not_2_out,
       not_3_out, not_4_out, not_5_out, not_6_out;

  not not_1 (not_1_out, A);
  not not_2 (not_2_out, B);
  not not_3 (not_3_out, A);
  not not_4 (not_4_out, VEM_1);
  not not_5 (not_5_out, B);
  not not_6 (not_6_out, VEM_1);
  and and_1 (and_1_out, B, VEM_1);
  and and_2 (and_2_out, A, VEM_1);
  and and_3 (and_3_out, A, B);
  and and_4 (and_4_out, not_1_out, not_2_out, VEM_1);
  and and_5 (and_5_out, not_3_out, B, not_4_out);
  and and_6 (and_6_out, A, not_5_out, not_6_out);
  and and_7 (and_7_out, A, B, VEM_1);
  or or_1 (Vai_1, and_1_out, and_2_out, and_3_out);
  or or_2 (Soma, and_4_out, and_5_out, and_6_out, and_7_out);
endmodule

module Add_4 (
  input  [3:0] B,
  input  [3:0] A,
  output overflow,
  output [3:0] out_4
);

  wire add_um_2_vai_1, add_um_3_vai_1, add_um_4_vai_1;

  // Probe on A
  ADD_UM add_um_1 (.A(A[3]), .B(B[3]), .VEM_1(add_um_2_vai_1), .Soma(out_4[3]), .Vai_1(overflow));
  ADD_UM add_um_2 (.A(A[2]), .B(B[2]), .VEM_1(add_um_3_vai_1), .Soma(out_4[2]), .Vai_1(add_um_2_vai_1));
  // Probe on out_4
  ADD_UM add_um_3 (.A(A[1]), .B(B[1]), .VEM_1(add_um_4_vai_1), .Soma(out_4[1]), .Vai_1(add_um_3_vai_1));
  ADD_UM add_um_4 (.A(A[0]), .B(B[0]), .VEM_1(1'b0), .Soma(out_4[0]), .Vai_1(add_um_4_vai_1));
  // Probe on B
endmodule

module OR_4_bit (
  input  [3:0] B,
  input  [3:0] A,
  output [3:0] SAIDA
);

  or or_1 (SAIDA[2], A[2], B[2]);
  or or_2 (SAIDA[3], A[3], B[3]);
  or or_3 (SAIDA[1], A[1], B[1]);
  or or_4 (SAIDA[0], A[0], B[0]);
endmodule

module \not  (
  input  [3:0] B,
  output [3:0] SAIDA
);

  not not_1 (SAIDA[3], B[3]);
  not not_2 (SAIDA[2], B[2]);
  not not_3 (SAIDA[1], B[1]);
  not not_4 (SAIDA[0], B[0]);
endmodule

module Buffer_4b (
  input  [3:0] B,
  input  C,
  output [3:0] SAIDA
);

  assign SAIDA[3] = C ? B[3] : 1'bz;  // Controlled_Buffer controlled_buffer_1
  assign SAIDA[0] = C ? B[0] : 1'bz;  // Controlled_Buffer controlled_buffer_2
  assign SAIDA[2] = C ? B[2] : 1'bz;  // Controlled_Buffer controlled_buffer_3
  assign SAIDA[1] = C ? B[1] : 1'bz;  // Controlled_Buffer controlled_buffer_4
endmodule

module dec3X8 (
  input  [2:0] \Operação ,
  output a,
  output b,
  output c,
  output d,
  output e,
  output f,
  output g,
  output h
);

  wire not_1_out, not_2_out, not_3_out, not_4_out, not_5_out, not_6_out, not_7_out, not_8_out, not_9_out,
       not_10_out, not_11_out, not_12_out;

  not not_1 (not_1_out, \Operação [2]);
  not not_2 (not_2_out, \Operação [1]);
  not not_3 (not_3_out, \Operação [0]);
  not not_4 (not_4_out, \Operação [2]);
  not not_5 (not_5_out, \Operação [1]);
  not not_6 (not_6_out, \Operação [2]);
  not not_7 (not_7_out, \Operação [0]);
  not not_8 (not_8_out, \Operação [2]);
  not not_9 (not_9_out, \Operação [1]);
  not not_10 (not_10_out, \Operação [0]);
  not not_11 (not_11_out, \Operação [1]);
  not not_12 (not_12_out, \Operação [0]);
  and and_1 (h, \Operação [2], \Operação [1], \Operação [0]);
  and and_2 (a, not_1_out, not_2_out, not_3_out);
  and and_3 (b, not_4_out, not_5_out, \Operação [0]);
  and and_4 (c, not_6_out, \Operação [1], not_7_out);
  and and_5 (d, not_8_out, \Operação [1], \Operação [0]);
  and and_6 (e, \Operação [2], not_9_out, not_10_out);
  and and_7 (f, \Operação [2], not_11_out, \Operação [0]);
  and and_8 (g, \Operação [2], \Operação [1], not_12_out);
endmodule

module rot_left (
  input  [3:0] A_B_C_D,
  input  [1:0] X_Y,
  output [3:0] A_B_C_D_2
);

  wire and_1_out, and_2_out, and_3_out, and_4_out, and_5_out, and_6_out, and_7_out, and_8_out, and_9_out;

  and and_1 (and_1_out, ~X_Y[1], ~X_Y[0], A_B_C_D[3]);  // AND_Gate
  and and_2 (and_2_out, ~X_Y[1], X_Y[0], A_B_C_D[2]);  // AND_Gate
  and and_3 (and_3_out, X_Y[1], ~X_Y[0], A_B_C_D[1]);  // AND_Gate
  and and_4 (and_4_out, X_Y[1], X_Y[0], A_B_C_D[0]);
  and and_5 (and_5_out, ~X_Y[1], ~X_Y[0], A_B_C_D[2]);  // AND_Gate
  and and_6 (and_6_out, ~X_Y[1], X_Y[0], A_B_C_D[1]);  // AND_Gate
  and and_7 (and_7_out, X_Y[1], ~X_Y[0], A_B_C_D[0]);  // AND_Gate
  and and_8 (and_8_out, ~X_Y[1], ~X_Y[0], A_B_C_D[1]);  // AND_Gate
  and and_9 (and_9_out, ~X_Y[1], X_Y[0], A_B_C_D[0]);  // AND_Gate
  and and_10 (A_B_C_D_2[0], ~X_Y[1], ~X_Y[0], A_B_C_D[0]);  // AND_Gate
  or or_1 (A_B_C_D_2[3], and_1_out, and_2_out, and_3_out, and_4_out);
  or or_2 (A_B_C_D_2[2], and_5_out, and_6_out, and_7_out);
  or or_3 (A_B_C_D_2[1], and_8_out, and_9_out);
endmodule

module rot_right (
  input  [3:0] D_C_B_A,
  input  [1:0] X_Y,
  output [3:0] out_3
);

  wire and_1_out, and_2_out, and_3_out, and_4_out, and_5_out, and_6_out, and_7_out, and_8_out, and_9_out;

  and and_1 (and_1_out, ~X_Y[1], ~X_Y[0], D_C_B_A[0]);  // AND_Gate
  and and_2 (and_2_out, ~X_Y[1], X_Y[0], D_C_B_A[1]);  // AND_Gate
  and and_3 (and_3_out, X_Y[1], ~X_Y[0], D_C_B_A[2]);  // AND_Gate
  and and_4 (and_4_out, X_Y[1], X_Y[0], D_C_B_A[3]);
  and and_5 (and_5_out, ~X_Y[1], ~X_Y[0], D_C_B_A[1]);  // AND_Gate
  and and_6 (and_6_out, ~X_Y[1], X_Y[0], D_C_B_A[2]);  // AND_Gate
  and and_7 (and_7_out, X_Y[1], ~X_Y[0], D_C_B_A[3]);  // AND_Gate
  and and_8 (and_8_out, ~X_Y[1], ~X_Y[0], D_C_B_A[2]);  // AND_Gate
  and and_9 (and_9_out, ~X_Y[1], X_Y[0], D_C_B_A[3]);  // AND_Gate
  and and_10 (out_3[3], ~X_Y[1], ~X_Y[0], D_C_B_A[3]);  // AND_Gate
  or or_1 (out_3[0], and_1_out, and_2_out, and_3_out, and_4_out);
  or or_2 (out_3[1], and_5_out, and_6_out, and_7_out);
  or or_3 (out_3[2], and_8_out, and_9_out);
endmodule

module sub_trator (
  input  A,
  input  B,
  input  VEM_1,
  output S,
  output VAI_1
);

  wire and_1_out, and_2_out, and_3_out, and_4_out, and_5_out, and_6_out, and_7_out, not_1_out, not_2_out,
       not_3_out, not_4_out, not_5_out, not_6_out, not_7_out, not_8_out;

  not not_1 (not_1_out, A);
  not not_2 (not_2_out, B);
  not not_3 (not_3_out, A);
  not not_4 (not_4_out, VEM_1);
  not not_5 (not_5_out, B);
  not not_6 (not_6_out, VEM_1);
  not not_7 (not_7_out, A);
  not not_8 (not_8_out, A);
  and and_1 (and_1_out, not_1_out, not_2_out, VEM_1);
  and and_2 (and_2_out, not_3_out, B, not_4_out);
  and and_3 (and_3_out, A, not_5_out, not_6_out);
  and and_4 (and_4_out, A, B, VEM_1);
  and and_5 (and_5_out, not_7_out, VEM_1);
  and and_6 (and_6_out, not_8_out, B);
  or or_1 (VAI_1, and_5_out, and_6_out, and_7_out);
  and and_7 (and_7_out, B, VEM_1);
  or or_2 (S, and_1_out, and_2_out, and_3_out, and_4_out);
endmodule

module sub_4b (
  input  [3:0] B,
  input  [3:0] A,
  output overflow,
  output [3:0] out_4
);

  wire sub_trator_2_vai_1, sub_trator_3_vai_1, sub_trator_4_vai_1;

  // Probe on A
  sub_trator sub_trator_1 (.A(A[3]), .B(B[3]), .VEM_1(sub_trator_2_vai_1), .S(out_4[3]), .VAI_1(overflow));
  sub_trator sub_trator_2 (.A(A[2]), .B(B[2]), .VEM_1(sub_trator_3_vai_1), .S(out_4[2]), .VAI_1(sub_trator_2_vai_1));
  // Probe on out_4
  sub_trator sub_trator_3 (.A(A[1]), .B(B[1]), .VEM_1(sub_trator_4_vai_1), .S(out_4[1]), .VAI_1(sub_trator_3_vai_1));
  sub_trator sub_trator_4 (.A(A[0]), .B(B[0]), .VEM_1(1'b0), .S(out_4[0]), .VAI_1(sub_trator_4_vai_1));
  // Probe on B
endmodule

module ULA (
  input  DIRECIONADOR,
  input  [3:0] B,
  input  [3:0] A,
  input  [2:0] OPERADOR,
  output OVERFLOW,
  output [3:0] SAIDA,
  output ZERO
);

  wire add_4_1_overflow, and_1_out, and_2_out, dec3x8_1_a, dec3x8_1_b, dec3x8_1_c, dec3x8_1_d, dec3x8_1_e,
       dec3x8_1_f, dec3x8_1_g, dec3x8_1_h, not_2_out, sub_4b_1_overflow;
  wire [3:0] add_4_1_out_4, buffer_4b_6_saida, not_1_saida, or_4_bit_1_saida, rot_left_1_a_b_c_d_2,
       rot_right_1_out_3, sub_4b_1_out_4;

  or or_1 (OVERFLOW, and_1_out, and_2_out);
  and and_1 (and_1_out, add_4_1_overflow, dec3x8_1_b);
  and and_2 (and_2_out, sub_4b_1_overflow, dec3x8_1_c);
  dec3X8 dec3x8_1 (
    .a(dec3x8_1_a), .b(dec3x8_1_b), .c(dec3x8_1_c), .d(dec3x8_1_d), .e(dec3x8_1_e), .f(dec3x8_1_f),
    .g(dec3x8_1_g), .h(dec3x8_1_h), .\Operação (OPERADOR));
  Buffer_4b buffer_4b_1 (.C(dec3x8_1_a), .B(B), .SAIDA(SAIDA));
  Add_4 add_4_1 (.A(A), .overflow(add_4_1_overflow), .B(B), .out_4(add_4_1_out_4));
  Buffer_4b buffer_4b_2 (.C(dec3x8_1_b), .B(add_4_1_out_4), .SAIDA(SAIDA));
  sub_4b sub_4b_1 (.A(A), .overflow(sub_4b_1_overflow), .B(B), .out_4(sub_4b_1_out_4));
  Buffer_4b buffer_4b_3 (.C(dec3x8_1_c), .B(sub_4b_1_out_4), .SAIDA(SAIDA));
  and and_3 (ZERO, ~SAIDA[0], ~SAIDA[1], ~SAIDA[2], ~SAIDA[3], ~dec3x8_1_g, ~dec3x8_1_h);  // AND_Gate
  OR_4_bit or_4_bit_1 (.A(A), .B(B), .SAIDA(or_4_bit_1_saida));
  Buffer_4b buffer_4b_4 (.C(dec3x8_1_d), .B(or_4_bit_1_saida), .SAIDA(SAIDA));
  \not  not_1 (.SAIDA(not_1_saida), .B(B));
  Buffer_4b buffer_4b_5 (.C(dec3x8_1_e), .B(not_1_saida), .SAIDA(SAIDA));
  rot_left rot_left_1 (.A_B_C_D(A), .X_Y(B[1:0]), .A_B_C_D_2(rot_left_1_a_b_c_d_2));
  rot_right rot_right_1 (.D_C_B_A(A), .X_Y(B[1:0]), .out_3(rot_right_1_out_3));
  not not_2 (not_2_out, DIRECIONADOR);
  Buffer_4b buffer_4b_6 (.C(not_2_out), .B(rot_left_1_a_b_c_d_2), .SAIDA(buffer_4b_6_saida));
  Buffer_4b buffer_4b_7 (.C(DIRECIONADOR), .B(rot_right_1_out_3), .SAIDA(buffer_4b_6_saida));
  Buffer_4b buffer_4b_8 (.C(dec3x8_1_f), .B(buffer_4b_6_saida), .SAIDA(SAIDA));
endmodule
